// Logisim project cpu.circ as structural Verilog: 2 circuits, main circuit main
module main (
);

  RAM #(.Select("low")) ram_1 ();  // open: addr, data, sel, clk, ld, clr

  // Notes on the sheet:
  //   16-BIT CPU
endmodule

module ProgramCounter (
  input  Clock,
  input  Reset,
  output [15:0] Adress,
  output [15:0] Adress__1
);

  Register #(.width(16), .Select("low")) register_1 (.D(Adress__1), .Q(Adress), .clk(Clock), .clr(Reset));  // open: en
  Adder #(.width(16)) adder_1 (.a(Adress), .b(16'h1), .out(Adress__1));  // open: cin, cout

  // Notes on the sheet:
  //   This module will point to an adress which executes the current instruction
endmodule
